# Fritzing sketch RV-Leveler (saved by Fritzing 0.9.3b)
circuit board: 4.28cm x 7.7cm
breadboards: 1

parts:
  ESP8266 = WeMos D1 Mini
  J1 = female pin header, 14 pins [form="♀ (female)"]
  J2 = Screw terminal - 2 pins [package=THT]
  12V5VBuck = female pin header, 4 pins [form="♀ (female)"]
  ADXL335 = female pin header, 5 pins [form="♀ (female)"]

nets:
  N1: ESP8266.3V3, J1.pin1, J1.pin8, ADXL335.pin1
  N2: ESP8266.5V, 12V5VBuck.pin1
  N3: ESP8266.D1, J1.pin3
  N4: ESP8266.D2, J1.pin5
  N5: ESP8266.D3, J1.pin11
  N6: ESP8266.D4, J1.pin14
  N7: ESP8266.D5, J1.pin7, J1.pin10
  N8: ESP8266.D6, J1.pin9, J1.pin13
  N9: ESP8266.D7, J1.pin6, J1.pin12
  N10: ESP8266.D8, ADXL335.pin2
  N11: ESP8266.G, J1.pin2, J2.pin2, 12V5VBuck.pin2, ADXL335.pin5
  N12: ESP8266.RST, J1.pin4
  N13: ESP8266.RX, ADXL335.pin3
  N14: ESP8266.TX, ADXL335.pin4
  N15: J2.pin1, 12V5VBuck.pin3

notes:
  http://www.thissmarthouse.com/rv/
