# Fritzing sketch RV-IoT (saved by Fritzing 0.9.3b)

parts:
  Raspberry_Pi_1 = Raspberry Pi 3 [part_number=RPI-3-V1.2]
  M1 = RioRand LM2596
  12V_Input = Power Jack [package=power_jack_pth_lock]
  RPi_On/Off = Round Pushbutton
  U2 = ESP8266 WiFi Module [part_number=ESP8266]
  neopixel1 = Neopixel Ring 16
  M2 = RioRand LM2596
  U3 = ESP8266 WiFi Module [part_number=ESP8266]
  neopixel2 = Neopixel Ring 16
  M3 = RioRand LM2596
  U4 = ESP8266 WiFi Module [part_number=ESP8266]
  neopixel3 = Neopixel Ring 16
  M4 = RioRand LM2596
  Manual_Lights_On = Taiway 100-SP-X-T1 SPDT Miniature Toggle Switch [part_number=100-SP-X-T1-0-0-B1-M1 package=THT]
  KY-1 = Keyes Relay [package=THT]
  D1 = bridge rectifier TO-269AA [package="TO-269AA [SMD]"]
  A/C_Input = Camdenboss CTB0158-2 [part_number=CTB0158-2 package=THT]
  U5 = Sharp PC817 [package=THT]
  R1 = Resistor [tolerance=±5% resistance=390k package=THT]
  R2 = Resistor [tolerance=±5% resistance=10k package=THT]
  JP1 = Header 3 [package=screwterminal-3.5mm-3_lock.007s]
  C1 = Electrolytic Capacitor [capacitance=1μF package="0405 [SMD, electrolytic]"]
  U6 = ESP8266 WiFi Module [part_number=ESP8266]
  M5 = RioRand LM2596
  RHT1 = Humidity and Temperature Sensor RHT03
  U7 = ESP8266 WiFi Module [part_number=ESP8266]
  M6 = RioRand LM2596
  KY-2 = Keyes Relay [package=THT]
  U8 = ESP8266 WiFi Module [part_number=ESP8266]
  M7 = RioRand LM2596
  RHT2 = Humidity and Temperature Sensor RHT03
  Part1 = Adafruit TSL2561 [part_number="Adafruit #439"]
  U9 = ESP8266 WiFi Module [part_number=ESP8266]
  M8 = RioRand LM2596
  U10 = ESP8266 WiFi Module [part_number=ESP8266]
  M9 = RioRand LM2596
  RHT3 = Humidity and Temperature Sensor RHT03
  KY-3 = Keyes Relay [package=THT]
  Compartment_Heater = Fan - Ventilador [package=THT]

nets:
  N1: Raspberry_Pi_1.GPIO3, RPi_On/Off.leg1
  N2: Raspberry_Pi_1.GND, M1.Pin_4, RPi_On/Off.leg0
  N3: Raspberry_Pi_1.GIPO17, KY-1.signal
  N4: Raspberry_Pi_1.5V, M1.Pin_3, KY-1.power, KY-2.power
  GND: M1.Pin_1, 12V_Input.GNDBREAK, M2.Pin_2, neopixel2.GND, M3.Pin_2, U4.GND, neopixel3.GND, M4.Pin_2, M4.Pin_4, KY-1.ground, M5.Pin_2, M6.Pin_2, KY-2.ground, M7.Pin_2, M8.Pin_2, M9.Pin_2, Compartment_Heater.GND
  N5: M1.Pin_2, 12V_Input.PWR, Manual_Lights_On.L1, KY-1.C, KY-2.C, KY-3.C
  VCC: U2.VCC, neopixel1.VCC, M2.Pin_3
  GND_2: U2.GND, neopixel1.GND, M2.Pin_4
  N6: U2.GPIO_5, neopixel1.IN
  N7: M2.Pin_1, M3.Pin_1, M4.Pin_1, Manual_Lights_On.L2, KY-1.NO
  VCC_2: U3.VCC, neopixel2.VCC, M3.Pin_3
  N8: U3.GND, M3.Pin_4
  N9: U3.GPIO_5, neopixel2.IN
  VCC_3: U4.VCC, neopixel3.VCC, M4.Pin_3
  N10: U4.GPIO_5, neopixel3.IN
  N11: D1.AC#0, A/C_Input.pin2
  N12: D1.AC#1, A/C_Input.pin1
  N13: D1.DC+, R1.Pin_0
  N14: D1.DC-, U5.Pin_2
  N15: U5.Pin_1, R1.Pin_1
  N16: U5.Pin_4, JP1.2, C1.+, U6.GPIO_12
  N17: U5.Pin_3, C1.-
  N18: R2.Pin_0, JP1.1, U6.VCC, M5.Pin_3
  N19: JP1.3, U6.GND, M5.Pin_4
  N20: M5.Pin_1, M6.Pin_1, KY-2.NO, M7.Pin_1, M8.Pin_1, M9.Pin_1
  VCC_4: RHT1.Vcc, U7.VCC, M6.Pin_3
  N21: RHT1.Data-signal, U7.GPIO_12
  N22: RHT1.GND_2, U7.GND, M6.Pin_4
  VCC_5: U8.VCC, M7.Pin_3, RHT2.Vcc
  N23: U8.GND, M7.Pin_4, RHT2.GND_2
  N24: U8.GPIO_12, RHT2.Data-signal
  VIN: Part1.VIN, U9.VCC, M8.Pin_3
  GND_3: Part1.GND, U9.GND, M8.Pin_4
  N25: Part1.SDA, U9.GPIO_2
  N26: Part1.SCL, U9.GPIO_15
  VCC_6: U10.VCC, M9.Pin_3, RHT3.Vcc, KY-3.power
  N27: U10.GND, M9.Pin_4, RHT3.GND_2, KY-3.ground
  N28: U10.GPIO_16, KY-3.signal
  N29: U10.GPIO_12, RHT3.Data-signal
  N30: KY-3.NO, Compartment_Heater.5V

notes:
  AC Detector Subsystem (monitors for shore power)
  Lighting Subsystem
  Power on/Off RPi
  RPi turns on subsystems after successful boot
  Manual over-ride to turn on subsystems
  Sensor Replay - Turns on once RPi has booted
  Indoor Temp / Humidity
  Outdoor Temp / Humidity
  Solar LUX Sensor
  Plumbing Temp Sensor & Heater

custom parts:
  Neopixel Ring 16: Neopixel Ring x16
  Keyes Relay: The Keyes 5V relay module is suitable for SCM development, home appliance control. It uses a 5V~12V TIL control signal which can control DC / AC signal.
  Adafruit TSL2561: The TSL2561 luminosity sensor is an advanced digital light sensor, ideal for use in a wide range of light situations. Compared to low cost CdS cells, this sensor is more precise, allowing for exact lux calculations and can be configured for different gain/timing ranges to detect light ranges from up to 0.1 - 40,000+ Lux on the fly. The best part of this sensor is that it contains both infrared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
  Fan - Ventilador: Ventilador de 2 pines, se encuentra comunmente en computadoras de escritorio
